# Fritzing sketch PowerConvert (saved by Fritzing 0.9.3b)
circuit board: 8.45972cm x 3.23912cm
breadboards: 1

parts:
  Input_Voltage = BC9VPC [package=bc9vpc]
  IC1 = Voltage Regulator [package=to-220-alt]
  C1 = Ceramic Capacitor [capacitance=0.47µF voltage=20V package="100 mil [THT, multilayer]"]
  C2 = Ceramic Capacitor [capacitance=100nF voltage=10V package="100 mil [THT, multilayer]"]

nets:
  N1: Input_Voltage.V+, IC1.IN, C1.0
  N2: Input_Voltage.V-, IC1.GND, C1.1, C2.0
  5V: IC1.OUT, C2.1

custom parts:
  Voltage Regulator: Voltage Regulator Standard 7805 5V regulator. IGO (Input Ground Output). Spark Fun Electronics SKU : COM-00107
