# Fritzing sketch Solinst-20170409 (saved by Fritzing 0.9.3b)
breadboards: 1

parts:
  DHT1 = DHT22 Humidity and Temperature Sensor
  U1 = SHT1x Humdity Sensor [package=sht1x]
  J1 = female pin header, 3 pins [form="♀ (female)"]
  J2 = female pin header, 2 pins [form="♀ (female)"]
  R1 = Resistor [tolerance=±5% resistance=10k package=THT]
  R2 = Resistor [tolerance=±5% resistance=10k package=THT]
  C1 = Ceramic Capacitor [capacitance=100nF package="100 mil [THT, multilayer]"]
  C2 = Ceramic Capacitor [capacitance=100nF package="100 mil [THT, multilayer]"]
  Part2 = Adafruit Pro Trinket 5V 16MHz [part_number="Adafruit #2000"]
  Raspberry_Pi1 = Raspberry Pi 2
  IC2 = Voltage Regulator [package=to-220-alt]

nets:
  VDD: DHT1.VDD, U1.VDD, R1.Pin_1, R2.Pin_1, Part2.+5V
  N1: DHT1.DATA, R2.Pin_0, Part2.D4
  GND: DHT1.GND, U1.GND, J1.pin1, J2.pin1, C1.0, C2.1, Part2.GND, Raspberry_Pi1.GND, IC2.GND
  N2: U1.DATA, R1.Pin_0, Part2.D6
  N3: U1.SCK, Part2.D5
  N4: J1.pin2, Part2.D8
  N5: J1.pin3, C1.1, Part2.VBAT, IC2.IN
  N6: J2.pin2, Part2.D3
  N7: C2.0, IC2.OUT
  N8: Part2.TXD, Raspberry_Pi1.GPIO15
  N9: Part2.RXD, Raspberry_Pi1.GPIO14

custom parts:
  Adafruit Pro Trinket 5V 16MHz: Trinket's got a big sister in town - the Pro Trinket 5V! Pro Trinket combines everything you love about Trinket with the familiarity of the common core Arduino chip, the ATmega328. It's like an Arduino Pro Mini with more pins and USB tossed in, so delicious. Trinket's a year old now, and while its been great to see tons of tiny projects, sometimes you just need more pins, more FLASH, and more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
  Voltage Regulator: Voltage Regulator Standard 7805 5V regulator. IGO (Input Ground Output). Spark Fun Electronics SKU : COM-00107
