# Fritzing sketch Solinst (saved by Fritzing 0.9.3b)
breadboards: 2

parts:
  Part1 = Adafruit Pro Trinket 5V 16MHz [part_number="Adafruit #2000"]
  Part2 = Adafruit BMP183
  DHT1 = DHT22 Humidity and Temperature Sensor
  Part3 = Lithium Ion Polymer Battery 3.7v 2500mAh [part_number=328]  # not connected
  Part4 = Adafruit FONA 3G Breakout [part_number="Adafruit #2691 and #2687"]
  Raspberry_Pi1 = Raspberry Pi 2  # not connected
  R1 = Resistor [tolerance=±5% resistance=10k package=THT]
  J2 = female pin header, 4 pins [form="♀ (female)"]
  J3 = female pin header, 3 pins [form="♀ (female)"]
  ANT1 = Antenna  # not connected
  ANT2 = Antenna  # not connected
  R2 = Resistor [tolerance=±5% resistance=10k package=THT]
  IC1 = Voltage Regulator [package=to-220-alt]
  C1 = Ceramic Capacitor [capacitance=0.47µF voltage=20V package="100 mil [THT, multilayer]"]
  C2 = Ceramic Capacitor [capacitance=100nF voltage=10V package="100 mil [THT, multilayer]"]
  Part5 = Adafruit Pi Cobbler Plus [part_number="Adafruit #2029"]

nets:
  GND: Part1.GND, Part2.GND, DHT1.GND, J2.pin2, J3.pin3, IC1.GND, C1.1, C2.0, Part5.GND
  +5V: Part1.+5V, Part2.VIN, DHT1.VDD, R1.Pin_0, J2.pin1, R2.Pin_0, IC1.OUT, C2.1, Part5.+5V
  N1: Part1.D8, Part2.SCK
  N2: Part1.D6, Part2.SDO
  N3: Part1.D5, Part2.SDI
  N4: Part1.D4, Part2.CS
  N5: Part1.D3, DHT1.DATA, R1.Pin_1
  N6: Part1.TXD, Part5.RXD
  N7: Part1.RXD, Part5.TXD
  N8: Part1.D11, J3.pin2
  N9: Part1.D12, J2.pin3
  N10: Part1.D13, J2.pin4, R2.Pin_1
  N11: Part4.+5V, Part4.Vio
  N12: Part4.Key, Part5.GPIO18
  N13: J3.pin1, IC1.IN, C1.0

custom parts:
  Adafruit Pro Trinket 5V 16MHz: Trinket's got a big sister in town - the Pro Trinket 5V! Pro Trinket combines everything you love about Trinket with the familiarity of the common core Arduino chip, the ATmega328. It's like an Arduino Pro Mini with more pins and USB tossed in, so delicious. Trinket's a year old now, and while its been great to see tons of tiny projects, sometimes you just need more pins, more FLASH, and more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
  Adafruit BMP183: Fans of the BMP085/BMP180 will want to take a look at the new BMP183 - an SPI spin on the old familiar classic. This precision sensor from Bosch is the best low-cost sensing solution for measuring barometric pressure and temperature. Because pressure changes with altitude you can also use it as an altimeter! The BMP183 is the next-generation of sensors from Bosch, and is the fraternal twin of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
  Lithium Ion Polymer Battery 3.7v 2500mAh: Lithium ion polymer (also known as 'lipo' or 'lipoly') batteries are thin, light and powerful. The output ranges from 4.2V when completely charged to 3.7V. This battery has a capacity of 2500mAh for a total of about 10 Wh. The batteries come pre-attached with a genuine 2-pin JST-PH connector as shown and include the necessary protection circuitry.
  Adafruit FONA 3G Breakout: For those who want to take it to the next level we now have a 3G Cellular Modem breakout! The FONA 3G has better coverage, GSM backwards-compatibility and even sports a built-in GPS module for geolocation & asset tracking. This all-in-one cellular phone module with that lets you add location-tracking, voice, text, SMS and data to your project in a single breakout.
  Voltage Regulator: Voltage Regulator Standard 7805 5V regulator. IGO (Input Ground Output). Spark Fun Electronics SKU : COM-00107
  Adafruit Pi Cobbler Plus: The Raspberry Pi B+/Pi 2/ Pi 3 has landed on the Maker World like a 40-GPIO pinned, quad-USB ported, credit card sized bomb of DIY joy. And while you can use most of our great Model B accessories by hooking up our downgrade cable, its probably a good time to upgrade your set up and accessorize using all of the Model B+'s / Pi 2's / Pi 3's 40 pins. That's why we now carry the Adafruit Assembled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
